# Fritzing sketch schematic (saved by Fritzing 1.0.1rc)
breadboards: 1

parts:
  Mod1 = Raspberry Pi 4B
  Part1 = Motor Driver 1A Dual TB6612FNG
  M1 = Dagu DGServo 9g (Top view) [part_number=RS001B]
  J1 = Dagu DGServo 9g header (male) [package=THT]
  M2 = RioRand LM2596
  U1 = SWITCH-SPST-2 [package=r_sw_th]
  U2 = SWITCH-SPST-2 [package=r_sw_th]
  U3 = LIPO-2000mAh [package=lipo-2000]
  Motor_with_encoder = Header 6 [package=molex-1x6_lock]

nets:
  N1: Mod1.3V3, Motor_with_encoder.3
  VCC: Mod1.5V, Part1.VCC, M1.vcc, J1.Vcc, M2.Pin_3
  GND: Mod1.GND, Part1.GND, M1.gnd, J1.gnd, M2.Pin_4, U2.O, Motor_with_encoder.4
  N2: Mod1.GPIO17, Motor_with_encoder.5
  N3: Mod1.GPIO18, M1.pulse, J1.pulse
  N4: Mod1.GPIO27, Motor_with_encoder.6
  N5: Mod1.GPIO22, U2.P
  N6: Mod1.GPIO23, Part1.AIN1
  N7: Mod1.GPIO24, Part1.AIN2
  N8: Mod1.GPIO25, Part1.STBY
  N9: Mod1.GPIO12, Part1.PWMA
  N10: Part1.A02, Motor_with_encoder.2
  N11: Part1.A01, Motor_with_encoder.1
  N12: Part1.VM, U1.O, U3.+
  N13: M2.Pin_1, U1.P
  N14: M2.Pin_2, U3.-
